# Fritzing sketch SEMACS (saved by Fritzing 0.9.3b)

parts:
  U1 = NodeMCU V1.0
  Grove1 = Grove OLED 128x96
  DHT1 = DHT11 Humitidy and Temperature Sensor
  DS1 = DS18B20 1-Wire Temperature Sensor [part_number=DS18B20]
  M1 = MAX30102
  GY1 = MPU-6050 Board GY-521 [form="♀ (female)" package=THT]
  R1 = Resistor [tolerance=±5% resistance=4.7k package=THT]
  R2 = Resistor [tolerance=±5% resistance=4.7k package=THT]
  R3 = Resistor [tolerance=±5% resistance=4.7k package=THT]
  S1 = Pushbutton [package="[THT]"]
  R4 = Resistor [tolerance=±5% resistance=100 package=THT]
  S2 = Pushbutton [package="[THT]"]
  R5 = Resistor [tolerance=±5% resistance=100 package=THT]

nets:
  N1: U1.D0, M1.INT
  N2: U1.D1, Grove1.SCL, M1.SCL, GY1.pin3, R1.Pin_0
  N3: U1.D2, Grove1.SDA, M1.SDA, GY1.pin4, R2.Pin_0
  N4: U1.D4, DS1.DQ, R3.Pin_0
  3V3: U1.3V3, DS1.VDD, GY1.pin1, R3.Pin_1
  GND: U1.GND, Grove1.GND, DHT1.GND, M1.GND, GY1.pin2, S1.Pin_3, S1.Pin_4, R4.Pin_1, S2.Pin_4, R5.Pin_1
  N5: U1.D5, DHT1.DATA
  N6: U1.D7, S1.Pin_1, R4.Pin_0
  N7: U1.D8, S2.Pin_1, R5.Pin_0
  VIN: U1.Vin, Grove1.VCC, DHT1.VDD, M1.VIN, R1.Pin_1, R2.Pin_1

custom parts:
  NodeMCU V1.0: ESP8266 based NodeMCU
  DHT11 Humitidy and Temperature Sensor: DHT11 Humidity and Temperature Sensor
  MAX30102: Oximeter module using the MAX30102 chip. You may wish to read (and check your module) this post on power problems with these modules: https://reedpaper.wordpress.com/2018/08/22/pulse-oximeter-max30100-max30102-how-to-fix-wrong-board/ . As usual, if you want the mounting holes in pcb, you need to drag a hole over the pad in silkscreen to actually drill the hole (by default they are not drilled)
  MPU-6050 Board GY-521: Acelerometro y Giroscopio MPU-6050 Board GY-521
