# Fritzing sketch ESP32_SEMACS (saved by Fritzing 0.9.3b)

parts:
  MH-ET_LIVE_ESP32_DEVKIT1 = MH-ET LIVE ESP32 DEVKIT 38 pins
  M1 = MAX30102
  GY1 = MPU-6050 Board GY-521 [form="♀ (female)" package=THT]
  Grove1 = Grove OLED 128x96
  DHT1 = DHT11 Humitidy and Temperature Sensor
  DS1 = DS18B20 1-Wire Temperature Sensor [part_number=DS18B20]
  R1 = Resistor [tolerance=±5% resistance=4.7k package=THT]
  R2 = Resistor [tolerance=±5% resistance=4.7k package=THT]
  R3 = Resistor [tolerance=±5% resistance=4.7k package=THT]
  U1 = LIPO-1000mAh [package=lipo-1000]
  TP1 = TP4056 [chip_label=TP4056 package="DIP (Dual Inline) [THT]"]

nets:
  VDD: MH-ET_LIVE_ESP32_DEVKIT1.5V, GY1.pin1, Grove1.VCC, DHT1.VDD, DS1.VDD, R1.Pin_0, R3.Pin_0, TP1.pin3
  GND: MH-ET_LIVE_ESP32_DEVKIT1.GND, M1.GND
  N1: MH-ET_LIVE_ESP32_DEVKIT1.IO23, M1.INT
  N2: MH-ET_LIVE_ESP32_DEVKIT1.IO22, GY1.pin4, Grove1.SCL
  N3: MH-ET_LIVE_ESP32_DEVKIT1.IO21, M1.SDA, GY1.pin3, Grove1.SDA, R2.Pin_1
  N4: MH-ET_LIVE_ESP32_DEVKIT1.IO5, DHT1.DATA
  N5: MH-ET_LIVE_ESP32_DEVKIT1.IO4, DS1.DQ, R3.Pin_1
  N6: M1.VIN, R2.Pin_0
  N7: M1.SCL, R1.Pin_1
  GND_2: GY1.pin2, Grove1.GND, DHT1.GND, DS1.GND
  N8: U1.+, TP1.pin4
  N9: U1.-, TP1.pin5

custom parts:
  MH-ET LIVE ESP32 DEVKIT 38 pins: http://mh.nodebb.com/topic/2/mh-et-live-esp32-devkit
  MAX30102: Oximeter module using the MAX30102 chip. You may wish to read (and check your module) this post on power problems with these modules: https://reedpaper.wordpress.com/2018/08/22/pulse-oximeter-max30100-max30102-how-to-fix-wrong-board/ . As usual, if you want the mounting holes in pcb, you need to drag a hole over the pad in silkscreen to actually drill the hole (by default they are not drilled)
  MPU-6050 Board GY-521: Acelerometro y Giroscopio MPU-6050 Board GY-521
  DHT11 Humitidy and Temperature Sensor: DHT11 Humidity and Temperature Sensor
  TP4056: A DIP stand-in part for whatever IC you want. With 6 pins on a 300mil dual inline package (DIP) footprint.
